# Fritzing sketch Balance_Robot_Wiring (saved by Fritzing 0.9.4)

parts:
  Pololu_A1 = Pololu A4988 [package=SO16]
  Pololu_A2 = Pololu A4988 [package=SO16]
  M1 = Stepper Motor - Bipolar
  M2 = Stepper Motor - Bipolar
  MPU9250_MPU-1 = SparkFun IMU Breakout - MPU-9250 [part_number=" SEN-13762"]
  LED1 = LED - 5mm [color="Yellow (595nm)" package="5 mm [THT]"]  # not connected
  LED2 = LED - 5mm [color="Yellow (595nm)" package="5 mm [THT]"]  # not connected
  LED3 = LED - 5mm [color="Yellow (595nm)" package="5 mm [THT]"]  # not connected
  3_Cell_LiPo = LIPO-2000mAh [part_number="3 Cell LiPo" package=lipo-2000]
  U1 = DC-DC_CONVERTER [package=dc-dc_converter]
  C1 = Electrolytic Capacitor [capacitance=1µF package="100 mil [THT, electrolytic]"]  # not connected
  C2 = Electrolytic Capacitor [capacitance=1µF package="100 mil [THT, electrolytic]"]  # not connected
  R1 = Resistor [tolerance=±20% resistance=220 package=THT]
  R2 = Resistor [tolerance=±20% resistance=220 package=THT]
  R3 = Resistor [tolerance=±20% resistance=220 package=THT]
  Part1 = Arduino Due (Rev2b)
  U2 = DC-DC_CONVERTER [package=dc-dc_converter]

nets:
  N1: Pololu_A1.MS2, Part1.D23
  N2: Pololu_A1.STEP, Part1.D5_PWM
  N3: Pololu_A1.DIR, Part1.D4_PWM/SS1
  N4: Pololu_A1.1B, M1.D
  N5: Pololu_A1.1A, M1.B
  N6: Pololu_A1.2A, M1.C
  N7: Pololu_A1.2B, M1.A
  GND: Pololu_A1.GND#14, MPU9250_MPU-1.GND, 3_Cell_LiPo.-, U1.GND1, Part1.GND, U2.GND1
  VIN: Pololu_A1.VMOT, Pololu_A2.VMOT, 3_Cell_LiPo.+, U1.VIN, U2.VIN
  N8: Pololu_A2.MS2, Part1.D22
  N9: Pololu_A2.STEP, Part1.D3_PWM
  N10: Pololu_A2.DIR, Part1.D2_PWM
  VDD: Pololu_A2.VDD, MPU9250_MPU-1.VDD, U2.VOUT
  N11: Pololu_A2.1B, M2.D
  N12: Pololu_A2.1A, M2.B
  N13: Pololu_A2.2A, M2.C
  N14: Pololu_A2.2B, M2.A
  N15: MPU9250_MPU-1.SCL/SCLK, Part1.D21/SCL3
  N16: MPU9250_MPU-1.SDA/SDI, Part1.D20/SDA3
  N17: U1.VOUT, Part1.VIN
  N18: R1.Pin_1, Part1.D13_PWM
  N19: R2.Pin_1, Part1.D12_PWM
  N20: R3.Pin_1, Part1.D11_PWM
